// Logisim project Milestone1_Solution.circ as structural Verilog: 3 circuits, main circuit main
module main (
  output [2:0] out_1,
  output out_2
);

  wire CLK, I, INC_PC, LD_AC, LD_AR, LD_DR, LD_IR, LD_PC, READ_MEM, WR_MEM;
  wire [3:0] ALU_SLCT;
  wire [11:0] AR, bit_extender_1_out, bit_extender_2_out, PC_q;
  wire [15:0] AC, alu_1_ac_output, bit_extender_3_out, bit_extender_4_out, DR_q, IR, multiplexer_1_out,
       ram_1_data, TR_q;

  Bit_Extender #(.in_width(16), .out_width(12)) bit_extender_1 (.in(multiplexer_1_out), .out(bit_extender_1_out));
  Bit_Extender #(.in_width(16), .out_width(12)) bit_extender_2 (.in(multiplexer_1_out), .out(bit_extender_2_out));
  CU cu_1 (
    .IR(IR), .CLK(CLK), .AC(AC), .AR(AR), .READ_MEM(READ_MEM), .LD_IR(LD_IR), .I(I), .LD_AR(LD_AR),
    .BUS_SLCT(out_1), .INC_PC(INC_PC), .LD_DR(LD_DR), .ALU_SLCT(ALU_SLCT), .LD_AC(LD_AC), .WR_MEM(WR_MEM),
    .LD_PC(LD_PC));
  Clock clock_1 (.out(CLK));
  Register #(.width(12)) u_AR (.D(bit_extender_1_out), .en(LD_AR), .Q(AR), .clk(CLK));  // open: clr
  Register #(.width(16)) TR (.D(multiplexer_1_out), .en(1'b0), .Q(TR_q), .clk(CLK));  // open: clr
  Register #(.width(16)) DR (.D(multiplexer_1_out), .en(LD_DR), .Q(DR_q), .clk(CLK));  // open: clr
  Register #(.width(16)) u_AC (.D(alu_1_ac_output), .en(LD_AC), .Q(AC), .clk(CLK));  // open: clr
  Counter #(.width(12), .max('hfff)) PC (
    .load(LD_PC), .D(bit_extender_2_out), .count(INC_PC), .Q(PC_q), .clk(CLK));  // open: carry, clr
  Register #(.width(16)) u_IR (.D(multiplexer_1_out), .en(LD_IR), .Q(IR), .clk(CLK));  // open: clr
  RAM #(.addrWidth(12), .dataWidth(16), .bus("separate")) ram_1 (
    .addr(AR), .din(multiplexer_1_out), .data(ram_1_data), .str(WR_MEM), .clk(CLK), .ld(READ_MEM));  // open: sel, clr
  assign bit_extender_3_out = {{4{1'b0}}, PC_q};  // Bit_Extender bit_extender_3
  assign bit_extender_4_out = {{4{1'b0}}, AR};  // Bit_Extender bit_extender_4
  ALU alu_1 (.A(DR_q), .B(AC), .in_3(ALU_SLCT), .E(out_2), .AC_Output(alu_1_ac_output));
  Multiplexer #(.select(3), .width(16), .enable("false")) multiplexer_1 (
    .in0(ram_1_data), .in1(bit_extender_4_out), .in2(TR_q), .in3(DR_q), .in4(AC), .in5(bit_extender_3_out),
    .in6(IR), .out(multiplexer_1_out), .sel(out_1));  // open: in7

  // Other names for the same wires on the sheet: BUS_SLCT[2:0] = out_1
endmodule

module ALU (
  input  [15:0] A,
  input  [15:0] B,
  input  [3:0] in_3,
  output E,
  output [15:0] AC_Output
);

  wire adder_1_cout, adder_2_cout, adder_3_cout, subtractor_1_bout, subtractor_2_bout;
  wire [15:0] adder_1_out, adder_2_out, adder_3_out, and_1_out, or_1_out, subtractor_1_out, subtractor_2_out,
       xor_1_out;

  Adder #(.width(16)) adder_1 (.a(A), .b(B), .out(adder_1_out), .cin(1'b0), .cout(adder_1_cout));
  Subtractor #(.width(16)) subtractor_1 (.a(A), .b(B), .out(subtractor_1_out), .bin(1'b0), .bout(subtractor_1_bout));
  assign and_1_out = A & B;  // AND_Gate and_1, 16 bits wide
  assign or_1_out = A | B;  // OR_Gate or_1, 16 bits wide
  assign xor_1_out = A ^ B;  // XOR_Gate xor_1, 16 bits wide
  Adder #(.width(16)) adder_2 (.a(A), .b({16{1'b0}}), .out(adder_2_out), .cin(1'b1), .cout(adder_2_cout));
  Subtractor #(.width(16)) subtractor_2 (.a(B), .b(A), .out(subtractor_2_out), .bout(subtractor_2_bout));  // open: bin
  Adder #(.width(16)) adder_3 (.a(B), .b({16{1'b0}}), .out(adder_3_out), .cin(1'b1), .cout(adder_3_cout));
  or or_2 (E, adder_1_cout, subtractor_1_bout, adder_2_cout, subtractor_2_bout, adder_3_cout);
  Multiplexer #(.select(4), .width(16)) multiplexer_1 (
    .in1(adder_1_out), .in2(subtractor_1_out), .in3(A), .in4(and_1_out), .in5(or_1_out), .in6(xor_1_out),
    .in7(adder_2_out), .in8(subtractor_2_out), .in9(adder_3_out), .out(AC_Output), .sel(in_3));  // open: in0, in10, in11, in12, in13, in14, in15, en
endmodule

// 1
module CU (
  input  [15:0] IR,
  input  CLK,
  input  [15:0] AC,
  input  [11:0] AR,
  output READ_MEM,
  output LD_IR,
  output I,
  output LD_AR,
  output [2:0] BUS_SLCT,
  output INC_PC,
  output LD_DR,
  output [3:0] ALU_SLCT,
  output LD_AC,
  output WR_MEM,
  output LD_PC
);

  wire CLR_SC, D0, D0_T3, D0_T4, D1, D1_T3, D1_T4, D2, D2_T3, D2_T4, D3, D4, D5, D5_T3, D5_T4, D6, D7,
       d_ff_1_q, I_t, not_1_out, r, r_b2, r_b2_zero_ac, r_b5, T0, T2, T3, T4, T5, T6, T7, T8, T9, T10, T11,
       T12, T13, T14, T15, ZERO_AC;
  wire [3:0] SC_q;

  D_Flip_Flop d_ff_1 (.clk(CLK), .D(CLR_SC), .Q(d_ff_1_q));  // open: Qn, preset, en, reset
  Decoder #(.select(4), .enable("false")) decoder_1 (
    .out0(T0), .out1(LD_IR), .out2(T2), .out3(T3), .out4(T4), .out5(T5), .out6(T6), .out7(T7), .out8(T8),
    .out9(T9), .out10(T10), .out11(T11), .out12(T12), .out13(T13), .out14(T14), .out15(T15), .sel(SC_q));
  Counter #(.width(4), .max('hf)) SC (.Q(SC_q), .clk(CLK), .clr(d_ff_1_q));  // open: load, D, count, carry
  D_Flip_Flop d_ff_2 (.clk(CLK), .D(IR[15]), .Q(I));  // open: Qn, preset, en, reset
  nor nor_1 (ZERO_AC, AC[0], AC[1], AC[2], AC[3], AC[4], AC[5], AC[6], AC[7], AC[9], AC[10], AC[11], AC[12], AC[13], AC[14], AC[15], AC[8]);
  Decoder #(.select(3), .enable("false")) decoder_2 (
    .out0(D0), .out1(D1), .out2(D2), .out3(D3), .out4(D4), .out5(D5), .out6(D6), .out7(D7), .sel(IR[14:12]));
  or u_CLR_SC (CLR_SC, D0_T4, D1_T4, D2_T4, WR_MEM, LD_PC, D5_T4, r);
  and and_1 (D0_T3, D0, T3);
  and and_2 (D0_T4, D0, T4);
  and and_3 (D1_T3, D1, T3);
  and and_4 (D1_T4, D1, T4);
  and and_5 (D2_T3, D2, T3);
  and and_6 (D2_T4, D2, T4);
  and and_7 (WR_MEM, D3, T3);
  not not_1 (not_1_out, I_t);
  or LD_MEM (READ_MEM, LD_IR, D0_T3, D1_T3, D2_T3, D5_T3);
  Priority_Encoder priority_encoder_1 (
    .in0(READ_MEM), .in1(LD_PC), .in4(WR_MEM), .in5(T0), .in6(T2), .out(BUS_SLCT));  // open: in2, in3, in7, en_in, gs, en_out
  or u_INC_PC (INC_PC, LD_IR, r_b2_zero_ac);
  or u_LD_DR (LD_DR, D0_T3, D1_T3, D2_T3, D2_T3, D5_T3);
  Priority_Encoder #(.select(4)) priority_encoder_2 (
    .in1(D1_T4), .in3(D2_T4), .in4(D0_T4), .in8(D5_T4), .in9(r_b5), .out(ALU_SLCT));  // open: in0, in2, in5, in6, in7, in10, in11, in12, in13, in14, in15, gs, en_out, en_in
  and and_8 (LD_PC, D4, T3);
  and and_9 (D5_T3, D5, T3);
  and and_10 (D5_T4, D5, T4);
  and and_11 (r, D7, T3, not_1_out);
  or u_LD_AR (LD_AR, T0, T2);
  or u_LD_AC (LD_AC, D0_T4, D1_T4, D2_T4, D5_T4, r_b5);
  and and_12 (r_b2, r, AR[2]);
  and and_13 (r_b5, r, AR[5]);
  and and_14 (r_b2_zero_ac, r_b2, ZERO_AC);

  // Other names for the same wires on the sheet: b2 = AR[2]; b5 = AR[5]; D3_T3 = WR_MEM; D4_T3 = LD_PC;
  //   RD_MEM = READ_MEM; T1 = LD_IR
endmodule
